// Logisim project latihan 1.circ as structural Verilog: 6 circuits, main circuit main
module main (
  input  A,
  input  B,
  output C,
  output D,
  output E
);

  not not_1 (C, A);
  and and_1 (D, A, B);
  or or_1 (E, A, B);
endmodule

module HA (
  input  A,
  input  B,
  output Sum,
  output Carry
);

  xor xor_1 (Sum, A, B);
  and and_1 (Carry, A, B);
endmodule

module FA (
  input  Cin,
  input  A,
  input  B,
  output Cout,
  output Sum
);

  wire ha_1_carry, ha_1_sum, ha_2_carry;

  HA ha_1 (.A(Cin), .B(A), .Sum(ha_1_sum), .Carry(ha_1_carry));
  HA ha_2 (.A(ha_1_sum), .B(B), .Sum(Sum), .Carry(ha_2_carry));
  or or_1 (Cout, ha_1_carry, ha_2_carry);
endmodule

module FA4 (
  input  Cin,
  input  A0,
  input  A1,
  input  A2,
  input  A3,
  input  B0,
  input  B1,
  input  B2,
  input  B3,
  output S0,
  output S1,
  output S2,
  output S3,
  output Cout
);

  wire fa_1_cout, fa_2_cout, fa_3_cout;

  FA fa_1 (.Cin(Cin), .A(A0), .B(B0), .Cout(fa_1_cout), .Sum(S0));
  FA fa_2 (.Cin(fa_1_cout), .A(A1), .B(B1), .Cout(fa_2_cout), .Sum(S1));
  FA fa_3 (.Cin(fa_2_cout), .A(A2), .B(B2), .Cout(fa_3_cout), .Sum(S2));
  FA fa_4 (.Cin(fa_3_cout), .A(A3), .B(B3), .Cout(Cout), .Sum(S3));
endmodule

module FA41 (
  input  Cin,
  input  [3:0] A,
  input  [3:0] B,
  output [3:0] Sum,
  output Cout
);

  // Probe on A
  // Probe on B
  FA4 fa4_1 (
    .Cin(Cin), .A0(A[0]), .A1(A[1]), .A2(A[2]), .A3(A[3]), .B0(B[0]), .B1(B[1]), .B2(B[2]), .B3(B[3]),
    .S0(Sum[0]), .S1(Sum[1]), .S2(Sum[2]), .S3(Sum[3]), .Cout(Cout));
  // Probe on Sum
endmodule

module FA81 (
  input  Cin,
  input  [7:0] A,
  input  [7:0] B,
  output [7:0] Sum,
  output Cout
);

  wire fa41_1_cout;

  // Probe on A
  // Probe on B
  FA41 fa41_1 (.Cin(Cin), .A(A[3:0]), .B(B[3:0]), .Sum(Sum[3:0]), .Cout(fa41_1_cout));
  FA41 fa41_2 (.Cin(fa41_1_cout), .A(A[7:4]), .B(B[7:4]), .Sum(Sum[7:4]), .Cout(Cout));
  // Probe on Sum
endmodule
